# Fritzing sketch bombardino (saved by Fritzing 0.8.4b)
circuit board: 16.9333cm x 5.64444cm
breadboards: 5

parts:
  J2 = shrouded pin header, 10 pins [form="♂ (shrouded male)"]  # not connected
  R1 = Rotary Potentiometer (Large) [maximum_resistance=100kΩ package=THT]
  S1 = Pushbutton [package="[THT]"]
  S2 = Pushbutton [package="[THT]"]
  R7 = Resistor [tolerance=±5% resistance=220 package=THT]
  R9 = Resistor [tolerance=±5% resistance=10k package=THT]
  R10 = Resistor [tolerance=±5% resistance=10k package=THT]
  R11 = Resistor [tolerance=±5% resistance=10k package=THT]
  R12 = Resistor [tolerance=±5% resistance=10k package=THT]
  R13 = Resistor [tolerance=±5% resistance=10k package=THT]
  S3 = Pushbutton [package="[THT]"]
  R14 = Resistor [tolerance=±5% resistance=1k package=THT]
  K1 = Relay [part_number=FRS1B-S package=THT]
  BAT1 = LIPO-110mAh [package=lipo-110]
  J3 = Piezo Speaker
  R6 = Resistor [tolerance=±5% resistance=1k package=THT]
  R8 = Resistor [tolerance=±5% resistance=1k package=THT]
  Componente2 = Triple Axis Accelerometer Breakout - ADXL335  # not connected
  X2 = USB Connectors [package=usb-a-s]
  LED1 = LED - 5mm [color="Red (633nm)" package="5 mm [THT]"]
  LED2 = LED - 5mm [color="Red (633nm)" package="5 mm [THT]"]
  LED3 = LED - 5mm [color="Red (633nm)" package="5 mm [THT]"]
  R15 = Resistor [tolerance=±5% resistance=1k package=THT]
  Arduino1 = Arduino Uno (Rev3)
  J4 = Piezo Speaker

nets:
  N1: R1.leg1, S1.Pin_3, S1.Pin_4, S2.Pin_3, S2.Pin_4, Arduino1.5V
  N2: R1.wiper, Arduino1.A0
  N3: R1.leg2, R9.Pin_1, R10.Pin_1, R11.Pin_1, R12.Pin_1, R13.Pin_1, K1.COIL1, K1.COIL2, R8.Pin_1, R15.Pin_1, Arduino1.GND, Arduino1.D8
  N4: S1.Pin_1, S1.Pin_2, R6.Pin_1
  N5: S2.Pin_1, S2.Pin_2, R7.Pin_1, R6.Pin_0
  N6: R9.Pin_0, R10.Pin_0, R11.Pin_0, R12.Pin_0, R13.Pin_0, S3.Pin_3, S3.Pin_4, Arduino1.D2, Arduino1.D3_PWM, Arduino1.D4, Arduino1.D5_PWM, Arduino1.D6_PWM
  N7: S3.Pin_1, S3.Pin_2, R14.Pin_0, R14.Pin_1, Arduino1.D7
  N8: K1.A, K1.B, J3.pin2
  N9: K1.C1, K1.C2, BAT1.+
  N10: BAT1.-, J3.pin1
  N11: R8.Pin_0, Arduino1.A5/SCL
  N12: X2.D-, Arduino1.A4/SDA
  N13: LED1.cathode, LED2.cathode, LED3.cathode, Arduino1.D9_PWM
  N14: LED1.anode, LED2.anode, LED3.anode, R15.Pin_0
  N15: Arduino1.D10_PWM/SS, J4.pin2

notes:
  pin 1 VCC
  pin2 GND
  pin3 CLK
  pin4 DATA
  pin5 STB1
  Sirena
  piezo su piede 10!
